# Fritzing sketch BasicLEDPattern (saved by Fritzing 0.4.3b)
breadboards: 1

parts:
  R1 = Resistor [resistance=1k package=THT]
  VCC1 = obsolete Battery
  LED1 = Red LED - 5mm
  S1 = Tilt Switch [package=THT]

nets:
  N1: R1.Pin_0, S1.Pin_2
  N2: R1.Pin_1, VCC1.+
  N3: VCC1.-, LED1.cathode
  N4: LED1.anode, S1.Pin_1
