# Fritzing sketch BasicLEDPotentionmeter (saved by Fritzing 0.5.2b)
breadboards: 1

parts:
  VCC1 = Battery block 9V
  R1 = Resistor [resistance=1k package=THT]
  LED1 = Red LED - 5mm
  R2 = Rotary Potentiometer (Large) [package=THT]

nets:
  N1: VCC1.-, R2.leg1
  N2: VCC1.+, R2.leg2
  N3: R1.Pin_0, R2.wiper
  N4: R1.Pin_1, LED1.anode
