# Fritzing sketch CapacitorLED (saved by Fritzing 0.8.5b)
breadboards: 1

parts:
  R1 = Resistor [resistance=1k tolerance=±5% package=THT]
  R2 = Resistor [resistance=10k tolerance=±5% package=THT]
  LED1 = LED - 5mm [color="Red (633nm)" package="5 mm [THT]"]
  C1 = Electrolytic Capacitor [capacitance=1000µF package="300 mil [THT, electrolytic]"]
  VCC1 = Battery block 9V
  S1 = Pushbutton [package=THT]

nets:
  N1: R1.Pin_0, S1.leg0
  N2: R1.Pin_1, VCC1.+
  N3: R2.Pin_0, C1.-
  N4: R2.Pin_1, VCC1.-
  N5: LED1.cathode, C1.+
  N6: LED1.anode, S1.leg1
