# Fritzing sketch CapacitorParallelLED (saved by Fritzing 0.8.5b)
breadboards: 1

parts:
  R1 = Resistor [resistance=1k tolerance=±5% package=THT]
  VCC1 = Battery block 9V
  C1 = Electrolytic Capacitor [capacitance=1000µF package="300 mil [THT, electrolytic]"]
  S1 = Pushbutton [package=THT]
  LED1 = LED - 5mm [color="Red (633nm)" package="5 mm [THT]"]

nets:
  N1: R1.Pin_0, S1.leg0
  N2: R1.Pin_1, VCC1.+, C1.+
  N3: VCC1.-, C1.-, LED1.cathode
  N4: S1.leg1, LED1.anode
