# Fritzing sketch CapictorInSeriesandParallel (saved by Fritzing 0.8.5b)
breadboards: 1

parts:
  R1 = Resistor [resistance=1k tolerance=±5% package=THT]
  C1 = Electrolytic Capacitor [capacitance=1000µF package="300 mil [THT, electrolytic]"]
  LED1 = LED - 5mm [color="Red (633nm)" package="5 mm [THT]"]
  C2 = Electrolytic Capacitor [capacitance=1µF package="100 mil [THT, electrolytic]"]
  VCC1 = Battery block 9V
  S3 = Pushbutton [package=THT]
  S4 = Pushbutton [package=THT]

nets:
  N1: R1.Pin_0, C2.-
  N2: R1.Pin_1, LED1.anode
  N3: C1.-, LED1.cathode, S4.leg1
  N4: C1.+, VCC1.+, S3.leg0
  N5: C2.+, S3.leg1
  N6: VCC1.-, S4.leg0
