# Fritzing sketch LEDTransitorBlink (saved by Fritzing 0.8.5b)
breadboards: 1

parts:
  VCC1 = Battery block 9V
  R1 = Resistor [tolerance=±5% resistance=1k package=THT]
  R2 = Resistor [tolerance=±5% resistance=220 package=THT]
  LED1 = LED - 5mm [color="Red (633nm)" package="5 mm [THT]"]
  Q1 = NPN-Transistor [package="TO92 [THT]"]
  C1 = Electrolytic Capacitor [capacitance=0.1mF package="100 mil [THT, electrolytic]"]

nets:
  N1: VCC1.-, LED1.cathode, C1.-
  N2: VCC1.+, R1.Pin_1
  N3: R1.Pin_0, Q1.E, C1.+
  N4: R2.Pin_0, Q1.C
  N5: R2.Pin_1, LED1.anode
