# Fritzing sketch npnMotorTransistor (saved by Fritzing 0.5.2b)
breadboards: 1

parts:
  R9 = Resistor [resistance=330 package=THT]
  LED8 = Red LED - 5mm
  R8 = Resistor [resistance=10k package=THT]
  VCC1 = Battery block 9V
  S1 = Pushbutton [package="[THT]"]
  M1 = DC Motor
  VCC1_2 = Battery block 9V
  Q1 = NPN-Transistor [package="TO92 [THT]"]

nets:
  N1: R9.Pin_0, LED8.anode
  N2: R9.Pin_1, M1.pin_1
  N3: LED8.cathode, Q1.C
  N4: R8.Pin_0, S1.Pin_1, S1.Pin_2
  N5: R8.Pin_1, Q1.B
  N6: VCC1.-, VCC1_2.-, Q1.E
  N7: VCC1.+, S1.Pin_3, S1.Pin_4
  N8: M1.pin_2, VCC1_2.+
